// Logisim project control-logic.circ as structural Verilog: 1 circuit, main circuit control_logic
module control_logic (
  input  [31:0] Instruction,
  input  BrEq,
  input  BrLt,
  output PCSel,
  output RegWEn,
  output [2:0] ImmSel,
  output BrUn,
  output ASel,
  output BSel,
  output [3:0] ALUSel,
  output MemWEn,
  output [1:0] WBSel
);

  wire add, addi, and_1, and_1_out, and_2_out, and_3_out, and_4_out, and_13_out, and_18_out, and_19_out,
       and_20_out, and_24_out, and_25_out, and_29_out, and_30_out, and_31_out, and_32_out, and_37_out,
       and_41_out, andi, auipc, b_type, beq, bge, bgeu, blt, bltu, bne, comparator_1_eq, comparator_2_eq,
       comparator_4_eq, comparator_5_eq, comparator_6_eq, comparator_7_eq, comparator_8_eq, comparator_9_eq,
       comparator_10_eq, comparator_11_eq, comparator_12_eq, comparator_13_eq, comparator_14_eq,
       comparator_16_eq, comparator_17_eq, comparator_18_eq, comparator_19_eq, comparator_20_eq,
       comparator_21_eq, comparator_22_eq, comparator_23_eq, comparator_24_eq, comparator_25_eq,
       comparator_26_eq, comparator_27_eq, comparator_28_eq, comparator_29_eq, comparator_30_eq,
       comparator_31_eq, comparator_32_eq, comparator_33_eq, comparator_34_eq, comparator_35_eq,
       comparator_36_eq, comparator_37_eq, comparator_38_eq, comparator_39_eq, comparator_40_eq,
       comparator_41_eq, comparator_42_eq, comparator_43_eq, comparator_47_eq, comparator_48_eq,
       comparator_51_eq, comparator_52_eq, comparator_53_eq, i_type, jal, jalr, l_type, lb, lh, lui, lw, mul,
       mulh, mulhu, not_1_out, not_2_out, not_3_out, or_1, or_1_out, or_3_out, ori, priority_encoder_1_gs,
       r_type, s_type, sb, sh, sll_1, slli, slt, slti, sra_1, srai, srl_1, srli, sub, sw, xor_1, xori;
  wire [2:0] priority_encoder_1_out;
  wire [4:0] priority_encoder_2_out;
  wire [5:0] adder_1_out, bit_extender_1_out, bit_extender_2_out, res;
  wire [15:14] rom_1_data;

  Comparator #(.width(3)) comparator_1 (.a(Instruction[14:12]), .b(3'b000), .eq(comparator_1_eq));  // open: gt, lt
  Comparator #(.width(3)) comparator_2 (.a(Instruction[14:12]), .b(3'b000), .eq(comparator_2_eq));  // open: gt, lt
  Comparator #(.width(7)) comparator_3 (.a(Instruction[6:0]), .b(7'b0100011), .eq(s_type));  // open: gt, lt
  Comparator #(.width(3)) comparator_4 (.a(Instruction[14:12]), .b(3'b000), .eq(comparator_4_eq));  // open: gt, lt
  Comparator #(.width(3)) comparator_5 (.a(Instruction[14:12]), .b(3'b101), .eq(comparator_5_eq));  // open: gt, lt
  ROM #(.addrWidth(6), .dataWidth(16)) rom_1 (
    .addr(res), .data({rom_1_data, WBSel, MemWEn, ALUSel, BSel, ASel, BrUn, ImmSel, RegWEn}));
  and u_and_1 (and_1_out, r_type, comparator_1_eq);
  Comparator #(.width(7)) comparator_6 (.a(Instruction[31:25]), .b({7{1'b0}}), .eq(comparator_6_eq));  // open: gt, lt
  and and_2 (and_2_out, r_type, comparator_2_eq);
  Comparator #(.width(7)) comparator_7 (.a(Instruction[31:25]), .b(7'b0100000), .eq(comparator_7_eq));  // open: gt, lt
  and and_3 (and_3_out, r_type, comparator_4_eq);
  Comparator #(.width(7)) comparator_8 (.a(Instruction[31:25]), .b(7'b0000001), .eq(comparator_8_eq));  // open: gt, lt
  and and_4 (and_4_out, r_type, comparator_5_eq);
  Comparator #(.width(7)) comparator_9 (.a(Instruction[31:25]), .b({7{1'b0}}), .eq(comparator_9_eq));  // open: gt, lt
  Comparator #(.width(3)) comparator_10 (.a(Instruction[14:12]), .b(3'b111), .eq(comparator_10_eq));  // open: gt, lt
  Comparator #(.width(3)) comparator_11 (.a(Instruction[14:12]), .b(3'b100), .eq(comparator_11_eq));  // open: gt, lt
  Comparator #(.width(3)) comparator_12 (.a(Instruction[14:12]), .b(3'b110), .eq(comparator_12_eq));  // open: gt, lt
  Comparator #(.width(3)) comparator_13 (.a(Instruction[14:12]), .b(3'b001), .eq(comparator_13_eq));  // open: gt, lt
  and and_5 (add, and_1_out, comparator_6_eq);
  and and_6 (sub, and_2_out, comparator_7_eq);
  and and_7 (mul, and_3_out, comparator_8_eq);
  and and_8 (srl_1, and_4_out, comparator_9_eq);
  Comparator #(.width(3)) comparator_14 (.a(Instruction[14:12]), .b(3'b001), .eq(comparator_14_eq));  // open: gt, lt
  and and_9 (bgeu, b_type, comparator_10_eq);
  and and_10 (blt, b_type, comparator_11_eq);
  and and_11 (bltu, b_type, comparator_12_eq);
  and and_12 (bne, b_type, comparator_13_eq);
  Comparator #(.width(7)) comparator_15 (.a(Instruction[6:0]), .b(7'b0110011), .eq(r_type));  // open: gt, lt
  Comparator #(.width(3)) comparator_16 (.a(Instruction[14:12]), .b(3'b110), .eq(comparator_16_eq));  // open: gt, lt
  Comparator #(.width(3)) comparator_17 (.a(Instruction[14:12]), .b(3'b100), .eq(comparator_17_eq));  // open: gt, lt
  Comparator #(.width(3)) comparator_18 (.a(Instruction[14:12]), .b(3'b010), .eq(comparator_18_eq));  // open: gt, lt
  and and_13 (and_13_out, r_type, comparator_14_eq);
  Comparator #(.width(7)) comparator_19 (
    .a(Instruction[31:25]), .b(7'b0000001), .eq(comparator_19_eq));  // open: gt, lt
  and and_14 (ori, i_type, comparator_16_eq);
  and and_15 (xori, i_type, comparator_17_eq);
  and and_16 (slti, i_type, comparator_18_eq);
  Comparator #(.width(3)) comparator_20 (.a(Instruction[14:12]), .b(3'b001), .eq(comparator_20_eq));  // open: gt, lt
  Comparator #(.width(3)) comparator_21 (.a(Instruction[14:12]), .b(3'b101), .eq(comparator_21_eq));  // open: gt, lt
  Comparator #(.width(3)) comparator_22 (.a(Instruction[14:12]), .b(3'b101), .eq(comparator_22_eq));  // open: gt, lt
  and and_17 (mulh, and_13_out, comparator_19_eq);
  and and_18 (and_18_out, i_type, comparator_20_eq);
  and and_19 (and_19_out, i_type, comparator_21_eq);
  and and_20 (and_20_out, i_type, comparator_22_eq);
  Comparator #(.width(3)) comparator_23 (.a(Instruction[14:12]), .b(3'b000), .eq(comparator_23_eq));  // open: gt, lt
  Comparator #(.width(3)) comparator_24 (.a(Instruction[14:12]), .b(3'b001), .eq(comparator_24_eq));  // open: gt, lt
  Comparator #(.width(3)) comparator_25 (.a(Instruction[14:12]), .b(3'b010), .eq(comparator_25_eq));  // open: gt, lt
  Comparator #(.width(7)) comparator_26 (.a(Instruction[31:25]), .b({7{1'b0}}), .eq(comparator_26_eq));  // open: gt, lt
  Comparator #(.width(7)) comparator_27 (.a(Instruction[31:25]), .b({7{1'b0}}), .eq(comparator_27_eq));  // open: gt, lt
  Comparator #(.width(7)) comparator_28 (
    .a(Instruction[31:25]), .b(7'b0100000), .eq(comparator_28_eq));  // open: gt, lt
  Comparator #(.width(3)) comparator_29 (.a(Instruction[14:12]), .b(3'b101), .eq(comparator_29_eq));  // open: gt, lt
  Comparator #(.width(3)) comparator_30 (.a(Instruction[14:12]), .b(3'b001), .eq(comparator_30_eq));  // open: gt, lt
  and and_21 (sb, s_type, comparator_23_eq);
  and and_22 (sh, s_type, comparator_24_eq);
  and and_23 (sw, s_type, comparator_25_eq);
  and and_24 (and_24_out, beq, BrEq);
  not not_1 (not_1_out, BrEq);
  and and_25 (and_25_out, blt, BrLt);
  Comparator #(.width(3)) comparator_31 (.a(Instruction[14:12]), .b(3'b000), .eq(comparator_31_eq));  // open: gt, lt
  Comparator #(.width(3)) comparator_32 (.a(Instruction[14:12]), .b(3'b111), .eq(comparator_32_eq));  // open: gt, lt
  and and_26 (slli, and_18_out, comparator_26_eq);
  and and_27 (srli, and_19_out, comparator_27_eq);
  and and_28 (srai, and_20_out, comparator_28_eq);
  and and_29 (and_29_out, r_type, comparator_29_eq);
  Comparator #(.width(7)) comparator_33 (
    .a(Instruction[31:25]), .b(7'b0100000), .eq(comparator_33_eq));  // open: gt, lt
  and and_30 (and_30_out, r_type, comparator_30_eq);
  Comparator #(.width(7)) comparator_34 (.a(Instruction[31:25]), .b({7{1'b0}}), .eq(comparator_34_eq));  // open: gt, lt
  and and_31 (and_31_out, bne, not_1_out);
  and and_32 (and_32_out, bltu, BrLt);
  and and_33 (addi, i_type, comparator_31_eq);
  and and_34 (andi, i_type, comparator_32_eq);
  and and_35 (sll_1, and_30_out, comparator_34_eq);
  and and_36 (sra_1, and_29_out, comparator_33_eq);
  not not_2 (not_2_out, BrLt);
  Comparator #(.width(3)) comparator_35 (.a(Instruction[14:12]), .b(3'b000), .eq(comparator_35_eq));  // open: gt, lt
  Comparator #(.width(3)) comparator_36 (.a(Instruction[14:12]), .b(3'b101), .eq(comparator_36_eq));  // open: gt, lt
  Comparator #(.width(3)) comparator_37 (.a(Instruction[14:12]), .b(3'b000), .eq(comparator_37_eq));  // open: gt, lt
  Comparator #(.width(3)) comparator_38 (.a(Instruction[14:12]), .b(3'b001), .eq(comparator_38_eq));  // open: gt, lt
  Comparator #(.width(3)) comparator_39 (.a(Instruction[14:12]), .b(3'b010), .eq(comparator_39_eq));  // open: gt, lt
  and and_37 (and_37_out, bge, not_2_out);
  not not_3 (not_3_out, BrLt);
  and and_38 (lb, l_type, comparator_37_eq);
  and and_39 (lh, l_type, comparator_38_eq);
  and and_40 (lw, l_type, comparator_39_eq);
  Comparator #(.width(3)) comparator_40 (.a(Instruction[14:12]), .b(3'b010), .eq(comparator_40_eq));  // open: gt, lt
  Comparator #(.width(3)) comparator_41 (.a(Instruction[14:12]), .b(3'b011), .eq(comparator_41_eq));  // open: gt, lt
  and and_41 (and_41_out, bgeu, not_3_out);
  Comparator #(.width(7)) comparator_42 (.a(Instruction[6:0]), .b(7'b0010011), .eq(comparator_42_eq));  // open: gt, lt
  Comparator #(.width(7)) comparator_43 (.a(Instruction[6:0]), .b(7'b1100111), .eq(comparator_43_eq));  // open: gt, lt
  Comparator #(.width(7)) comparator_44 (.a(Instruction[6:0]), .b(7'b1100011), .eq(b_type));  // open: gt, lt
  Comparator #(.width(7)) comparator_45 (.a(Instruction[6:0]), .b(7'b0000011), .eq(l_type));  // open: gt, lt
  and and_42 (beq, b_type, comparator_35_eq);
  and and_43 (bge, b_type, comparator_36_eq);
  and and_44 (slt, r_type, comparator_40_eq);
  and and_45 (mulhu, r_type, comparator_41_eq);
  Comparator #(.width(7)) comparator_46 (.a(Instruction[6:0]), .b(7'b1101111), .eq(jal));  // open: gt, lt
  Comparator #(.width(7)) comparator_47 (.a(Instruction[6:0]), .b(7'b1100111), .eq(comparator_47_eq));  // open: gt, lt
  Comparator #(.width(3)) comparator_48 (.a(Instruction[14:12]), .b(3'b000), .eq(comparator_48_eq));  // open: gt, lt
  Comparator #(.width(7)) comparator_49 (.a(Instruction[6:0]), .b(7'b0010111), .eq(auipc));  // open: gt, lt
  Comparator #(.width(7)) comparator_50 (.a(Instruction[6:0]), .b(7'b0110111), .eq(lui));  // open: gt, lt
  or u_or_1 (or_1_out, and_37_out, and_41_out);
  or or_2 (i_type, comparator_42_eq, comparator_43_eq);
  and and_46 (jalr, comparator_47_eq, comparator_48_eq);
  or or_3 (or_3_out, and_24_out, and_31_out, and_25_out, and_32_out, or_1_out);
  Comparator #(.width(3)) comparator_51 (.a(Instruction[14:12]), .b(3'b111), .eq(comparator_51_eq));  // open: gt, lt
  Comparator #(.width(3)) comparator_52 (.a(Instruction[14:12]), .b(3'b110), .eq(comparator_52_eq));  // open: gt, lt
  Comparator #(.width(3)) comparator_53 (.a(Instruction[14:12]), .b(3'b100), .eq(comparator_53_eq));  // open: gt, lt
  and and_47 (and_1, r_type, comparator_51_eq);
  and and_48 (or_1, r_type, comparator_52_eq);
  and and_49 (xor_1, r_type, comparator_53_eq);
  or or_4 (PCSel, jal, or_3_out, jalr);
  Priority_Encoder priority_encoder_1 (
    .in2(auipc), .in3(lui), .in4(jal), .in5(jalr), .out(priority_encoder_1_out), .gs(priority_encoder_1_gs));  // open: in0, in1, in6, in7, en_in, en_out
  assign bit_extender_1_out = {{3{1'b0}}, priority_encoder_1_out};  // Bit_Extender bit_extender_1
  Priority_Encoder #(.select_enc(5)) priority_encoder_2 (
    .in0(add), .in1(mul), .in2(sub), .in3(sll_1), .in4(mulh), .in5(mulhu), .in6(slt), .in7(xor_1),
    .in8(srl_1), .in9(sra_1), .in10(or_1), .in11(and_1), .in12(lb), .in13(lh), .in14(lw), .in15(addi),
    .in16(slli), .in17(slti), .in18(xori), .in19(srli), .in20(srai), .in21(ori), .in22(andi), .in23(sb),
    .in24(sh), .in25(sw), .in26(beq), .in27(bne), .in28(blt), .in29(bge), .in30(bltu), .in31(bgeu),
    .out(priority_encoder_2_out));  // open: gs, en_out, en_in
  assign bit_extender_2_out = {{1{1'b0}}, priority_encoder_2_out};  // Bit_Extender bit_extender_2
  Adder #(.width(6)) adder_1 (.a(bit_extender_1_out), .b(6'b100000), .out(adder_1_out));  // open: cin, cout
  Multiplexer #(.width(6)) multiplexer_1 (
    .in0(bit_extender_2_out), .in1(adder_1_out), .out(res), .sel(priority_encoder_1_gs));

  // Other names for the same wires on the sheet: opcode[6:0] = Instruction[6:0]; funct3[2:0] = Instruction[14:12];
  //   funct7[6:0] = Instruction[31:25]

  // Notes on the sheet:
  //   INPUTS to your circuit
  //   Connect ROM Input here ->
  //   contents of rom_1 (hex, n*v repeats v):
  //   100f 140f 160f 108f 148f 158f 110f 120f 128f 168f 130f 138f 41 41 41 1041 10c1 1141 1241 12c1 16c1
  //   1341 13c1 3842 3842 3842 4*3064 3074 3074 1067 17c7 2069 2041
  //   ROM FOR CONTROL LOGIC
  //   DON'T CHANGE THE LOCATIONS OF THE INPUTS AND OUTPUTS!
  //   This is only if you choose to do the ROM option
  //   OUTPUT from your circuit
  //   Reminder: If using ROM, use combinational logic for PCSel
endmodule
