// Logisim project cpu.circ as structural Verilog: 1 circuit, main circuit cpu
module cpu (
  input  clk,
  input  [31:0] Instruction,
  input  [31:0] MemReadData,
  output [31:0] MemAddress,
  output [31:0] ProgramCounter,
  output [31:0] ra,
  output [31:0] sp,
  output [31:0] t0,
  output [31:0] t1,
  output [31:0] t2,
  output [31:0] s0,
  output [31:0] s1,
  output [31:0] a0,
  output [3:0] MemWriteMask,
  output [31:0] MemWriteData
);

  wire branch_comp_1_breq, branch_comp_1_brlt, control_logic_1_asel, control_logic_1_brun,
       control_logic_1_bsel, control_logic_1_memwen, control_logic_1_regwen, PCSel;
  wire [1:0] control_logic_1_wbsel;
  wire [2:0] control_logic_1_immsel;
  wire [3:0] control_logic_1_alusel;
  wire [15:0] bit_extender_1_out;
  wire [31:0] imm_gen_1_immediate, multiplexer_1_out, multiplexer_2_out, multiplexer_3_out, PC_4, ram_1_dout,
       regfile_1_readdata1, RS2, WB_RES;

  Adder #(.width(32)) adder_1 (.a(ProgramCounter), .b(32'h4), .out(PC_4));  // open: cin, cout
  Multiplexer #(.width(32)) multiplexer_1 (.in0(PC_4), .in1(MemAddress), .out(multiplexer_1_out), .sel(PCSel));
  Register #(.width(32)) PC (.D(multiplexer_1_out), .en(1'b1), .clk(clk), .Q(ProgramCounter));  // open: clr
  control_logic control_logic_1 (
    .Instruction(Instruction), .BrEq(branch_comp_1_breq), .BrLt(branch_comp_1_brlt), .PCSel(PCSel),
    .RegWEn(control_logic_1_regwen), .ImmSel(control_logic_1_immsel), .BrUn(control_logic_1_brun),
    .ASel(control_logic_1_asel), .BSel(control_logic_1_bsel), .ALUSel(control_logic_1_alusel),
    .MemWEn(control_logic_1_memwen), .WBSel(control_logic_1_wbsel));
  regfile regfile_1 (
    .ReadIndex1(Instruction[19:15]), .ReadIndex2(Instruction[24:20]), .WriteIndex(Instruction[11:7]),
    .WriteData(WB_RES), .RegWEn(control_logic_1_regwen), .clk(clk), .ra(ra), .sp(sp), .t0(t0), .t1(t1),
    .t2(t2), .s0(s0), .s1(s1), .a0(a0), .ReadData1(regfile_1_readdata1), .ReadData2(RS2));
  imm_gen imm_gen_1 (.Instruction(Instruction), .ImmSel(control_logic_1_immsel), .Immediate(imm_gen_1_immediate));
  branch_comp branch_comp_1 (
    .BrData1(regfile_1_readdata1), .BrData2(RS2), .BrUn(control_logic_1_brun), .BrEq(branch_comp_1_breq),
    .BrLt(branch_comp_1_brlt));
  Multiplexer #(.width(32)) multiplexer_2 (
    .in0(regfile_1_readdata1), .in1(ProgramCounter), .out(multiplexer_2_out), .sel(control_logic_1_asel));
  Multiplexer #(.width(32)) multiplexer_3 (
    .in0(RS2), .in1(imm_gen_1_immediate), .out(multiplexer_3_out), .sel(control_logic_1_bsel));
  alu alu_1 (.A(multiplexer_2_out), .B(multiplexer_3_out), .ALUSel(control_logic_1_alusel), .ALUResult(MemAddress));
  RAM #(.addrWidth(16), .dataWidth(32)) ram_1 (
    .addr(bit_extender_1_out), .oe(1'b1), .dout(ram_1_dout));  // open: we, clk, din
  Bit_Extender #(.in_width(32)) bit_extender_1 (.in(MemAddress), .out(bit_extender_1_out));
  partial_store partial_store_1 (
    .Instruction(Instruction), .MemAddress(MemAddress), .DataFromReg(RS2), .MemWEn(control_logic_1_memwen),
    .MemWriteMask(MemWriteMask), .DataToMem(MemWriteData));
  partial_load partial_load_1 (
    .Instruction(Instruction), .MemAddress(MemAddress), .DataFromMem(ram_1_dout), .DataToReg(MemReadData));
  Multiplexer #(.select(2), .width(32)) multiplexer_4 (
    .in0(MemReadData), .in1(MemAddress), .in2(PC_4), .out(WB_RES), .sel(control_logic_1_wbsel));  // open: in3

  // Other names for the same wires on the sheet: ALURes[31:0] = MemAddress; ASel1TUN[31:0] = ProgramCounter

  // Notes on the sheet:
  //   To IMEM
  //   IMEM (do **NOT** move this)
  //   From IMEM
  //   Inputs/Outputs for testing. Do **NOT** move these.
  //   It is OK to move the PC, RegFile, ALU, MEM, Branch Comp, Imm Gen, Partial Load, Partial Store and Control Logic to wherever is most convenient for you when constructing your CPU, and to delete this text
  //   To DMEM
  //   DMEM (do **NOT** move this)
  //   From DMEM
endmodule
