// Logisim project partial-store.circ as structural Verilog: 1 circuit, main circuit partial_store
module partial_store (
  input  [31:0] Instruction,
  input  [31:0] MemAddress,
  input  [31:0] DataFromReg,
  input  MemWEn,
  output [3:0] MemWriteMask,
  output [31:0] DataToMem
);

  wire [1:0] BOT_TWO_BITS;
  wire [3:0] multiplexer_4_out, multiplexer_5_out;
  wire [31:0] bit_extender_1_out, bit_extender_2_out, bit_extender_3_out, bit_extender_4_out,
       bit_extender_5_out, bit_extender_6_out, multiplexer_1_out, multiplexer_2_out, multiplexer_3_out,
       shifter_1_out, shifter_2_out, shifter_3_out, shifter_4_out;

  assign bit_extender_1_out = {{24{1'b0}}, DataFromReg[7:0]};  // Bit_Extender bit_extender_1
  assign bit_extender_2_out = {{24{1'b0}}, DataFromReg[7:0]};  // Bit_Extender bit_extender_2
  assign bit_extender_3_out = {{24{1'b0}}, DataFromReg[7:0]};  // Bit_Extender bit_extender_3
  Shifter #(.width(32)) shifter_1 (.in(bit_extender_1_out), .\dist (5'b10000), .out(shifter_1_out));
  assign bit_extender_4_out = {{24{1'b0}}, DataFromReg[7:0]};  // Bit_Extender bit_extender_4
  Shifter #(.width(32)) shifter_2 (.in(bit_extender_4_out), .\dist (5'b11000), .out(shifter_2_out));
  assign bit_extender_5_out = {{16{1'b0}}, DataFromReg[15:0]};  // Bit_Extender bit_extender_5
  assign bit_extender_6_out = {{16{1'b0}}, DataFromReg[15:0]};  // Bit_Extender bit_extender_6
  Shifter #(.width(32)) shifter_3 (.in(bit_extender_3_out), .\dist (5'b01000), .out(shifter_3_out));
  Shifter #(.width(32)) shifter_4 (.in(bit_extender_6_out), .\dist (5'b10000), .out(shifter_4_out));
  Multiplexer #(.select(2), .width(32)) multiplexer_1 (
    .in0(bit_extender_5_out), .in2(shifter_4_out), .out(multiplexer_1_out), .sel(BOT_TWO_BITS));  // open: in1, in3
  Multiplexer #(.select(2), .width(32)) multiplexer_2 (
    .in0(bit_extender_2_out), .in1(shifter_3_out), .in2(shifter_1_out), .in3(shifter_2_out),
    .out(multiplexer_2_out), .sel(BOT_TWO_BITS));
  Bit_Extender #(.in_width(32), .out_width(2)) bit_extender_7 (.in(MemAddress), .out(BOT_TWO_BITS));
  Multiplexer #(.select(3), .width(32)) multiplexer_3 (
    .in0(multiplexer_2_out), .in1(multiplexer_1_out), .in2(DataFromReg), .out(multiplexer_3_out),
    .sel(Instruction[14:12]));  // open: in3, in4, in5, in6, in7
  Demultiplexer #(.width(32)) demultiplexer_1 (.out1(DataToMem), .in(multiplexer_3_out), .sel(MemWEn));  // open: out0
  Multiplexer #(.select(2), .width(4)) multiplexer_4 (
    .in0(4'b0001), .in2(4'b0010), .in3(4'b0100), .out(multiplexer_4_out), .sel(BOT_TWO_BITS));  // open: in1
  Multiplexer #(.select(2), .width(4)) multiplexer_5 (
    .in0(4'b0011), .in2(4'b1100), .out(multiplexer_5_out));  // open: in1, in3, sel
  Multiplexer #(.select(3), .width(4)) multiplexer_6 (
    .in0(multiplexer_4_out), .in1(multiplexer_5_out), .in2(4'b1111), .out(MemWriteMask),
    .sel(Instruction[14:12]));  // open: in3, in4, in5, in6, in7

  // Other names for the same wires on the sheet: Funct3[2:0] = Instruction[14:12]

  // Notes on the sheet:
  //   INPUTS to your circuit
  //   DON'T CHANGE THE LOCATIONS OF THE INPUTS AND OUTPUTS!
  //   OUTPUT from your circuit
endmodule
