// Logisim project regfile.circ as structural Verilog: 1 circuit, main circuit regfile
module regfile (
  input  [4:0] rs1,
  input  [4:0] rs2,
  input  [4:0] rd,
  input  [31:0] Write_Data,
  input  RegWEn,
  input  clk,
  output [31:0] ra,
  output [31:0] sp,
  output [31:0] t0,
  output [31:0] t1,
  output [31:0] t2,
  output [31:0] s0,
  output [31:0] s1,
  output [31:0] a0,
  output [31:0] Read_Data_1,
  output [31:0] Read_Data_2
);

  wire a0c, rac, s0c, s1c, spc, t0c, t1c, t2c, x3c, x4c, x11c, x12c, x13c, x14c, x15c, x16c, x17c, x18c,
       x19c, x20c, x21c, x22c, x23c, x24c, x25c, x26c, x27c, x28c, x29c, x30c, x31c;
  wire [31:0] x3, x4, x11, x12, x13, x14, x15, x16, x17, x18, x19, x20, x21, x22, x23, x24, x25, x26, x27,
       x28, x29, x30, x31, zero;

  Register #(.width(32)) register_1 (.D(Write_Data), .en(rac), .clk(clk), .Q(ra));  // open: clr
  Register #(.width(32)) register_2 (.D(Write_Data), .en(spc), .clk(clk), .Q(sp));  // open: clr
  Register #(.width(32)) register_3 (.D(Write_Data), .en(t0c), .clk(clk), .Q(t0));  // open: clr
  Register #(.width(32)) register_4 (.D(Write_Data), .en(x3c), .clk(clk), .Q(x3));  // open: clr
  Register #(.width(32)) register_5 (.D(Write_Data), .en(x4c), .clk(clk), .Q(x4));  // open: clr
  Register #(.width(32)) register_6 (.D(Write_Data), .en(x11c), .clk(clk), .Q(x11));  // open: clr
  Register #(.width(32)) register_7 (.D(Write_Data), .en(x12c), .clk(clk), .Q(x12));  // open: clr
  Register #(.width(32)) register_8 (.D(Write_Data), .en(x13c), .clk(clk), .Q(x13));  // open: clr
  Register #(.width(32)) register_9 (.D(Write_Data), .en(x14c), .clk(clk), .Q(x14));  // open: clr
  Register #(.width(32)) register_10 (.D(Write_Data), .en(x15c), .clk(clk), .Q(x15));  // open: clr
  Register #(.width(32)) register_11 (.D(Write_Data), .en(t1c), .clk(clk), .Q(t1));  // open: clr
  Register #(.width(32)) register_12 (.D(Write_Data), .en(t2c), .clk(clk), .Q(t2));  // open: clr
  Register #(.width(32)) register_13 (.D(Write_Data), .en(s0c), .clk(clk), .Q(s0));  // open: clr
  Register #(.width(32)) register_14 (.D(Write_Data), .en(x16c), .clk(clk), .Q(x16));  // open: clr
  Register #(.width(32)) register_15 (.D(Write_Data), .en(x17c), .clk(clk), .Q(x17));  // open: clr
  Register #(.width(32)) register_16 (.D(Write_Data), .en(x18c), .clk(clk), .Q(x18));  // open: clr
  Register #(.width(32)) register_17 (.D(Write_Data), .en(x19c), .clk(clk), .Q(x19));  // open: clr
  Register #(.width(32)) register_18 (.D(Write_Data), .en(x21c), .clk(clk), .Q(x21));  // open: clr
  Multiplexer #(.enable("false"), .select(5), .width(32)) multiplexer_1 (
    .in0({32{1'b0}}), .in1(ra), .in2(sp), .in3(x3), .in4(x4), .in5(t0), .in6(t1), .in7(t2), .in8(s0),
    .in9(s1), .in10(a0), .in11(x11), .in12(x12), .in13(x13), .in14(x14), .in15(x15), .in16(x16), .in17(x17),
    .in18(x18), .in19(x19), .in20(x20), .in21(x21), .in22(x22), .in23(x23), .in24(x24), .in25(x25),
    .in26(x26), .in27(x27), .in28(x28), .in29(x29), .in30(x30), .in31(x31), .out(Read_Data_1), .sel(rs1));
  Register #(.width(32)) register_19 (.D(Write_Data), .en(x20c), .clk(clk), .Q(x20));  // open: clr
  Register #(.width(32)) register_20 (.D(Write_Data), .en(x22c), .clk(clk), .Q(x22));  // open: clr
  Register #(.width(32)) register_21 (.D(Write_Data), .en(s1c), .clk(clk), .Q(s1));  // open: clr
  Register #(.width(32)) register_22 (.D(Write_Data), .en(a0c), .clk(clk), .Q(a0));  // open: clr
  Register #(.width(32)) register_23 (.D({32{1'b0}}), .en(1'b1), .clk(clk), .Q(zero));  // open: clr
  Register #(.width(32)) register_24 (.D(Write_Data), .en(x23c), .clk(clk), .Q(x23));  // open: clr
  Register #(.width(32)) register_25 (.D(Write_Data), .en(x24c), .clk(clk), .Q(x24));  // open: clr
  Register #(.width(32)) register_26 (.D(Write_Data), .en(x25c), .clk(clk), .Q(x25));  // open: clr
  Register #(.width(32)) register_27 (.D(Write_Data), .en(x26c), .clk(clk), .Q(x26));  // open: clr
  Register #(.width(32)) register_28 (.D(Write_Data), .en(x27c), .clk(clk), .Q(x27));  // open: clr
  Register #(.width(32)) register_29 (.D(Write_Data), .en(x28c), .clk(clk), .Q(x28));  // open: clr
  Register #(.width(32)) register_30 (.D(Write_Data), .en(x29c), .clk(clk), .Q(x29));  // open: clr
  Multiplexer #(.enable("false"), .select(5), .width(32)) multiplexer_2 (
    .in0({32{1'b0}}), .in1(ra), .in2(sp), .in3(x3), .in4(x4), .in5(t0), .in6(t1), .in7(t2), .in8(s0),
    .in9(s1), .in10(a0), .in11(x11), .in12(x12), .in13(x13), .in14(x14), .in15(x15), .in16(x16), .in17(x17),
    .in18(x18), .in19(x19), .in20(x20), .in21(x21), .in22(x22), .in23(x23), .in24(x24), .in25(x25),
    .in26(x26), .in27(x27), .in28(x28), .in29(x29), .in30(x30), .in31(x31), .out(Read_Data_2), .sel(rs2));
  Register #(.width(32)) register_31 (.D(Write_Data), .en(x30c), .clk(clk), .Q(x30));  // open: clr
  Register #(.width(32)) register_32 (.D(Write_Data), .en(x31c), .clk(clk), .Q(x31));  // open: clr
  Demultiplexer #(.enable("false"), .select(5)) demultiplexer_1 (
    .out1(rac), .out2(spc), .out3(x3c), .out4(x4c), .out5(t0c), .out6(t1c), .out7(t2c), .out8(s0c),
    .out9(s1c), .out10(a0c), .out11(x11c), .out12(x12c), .out13(x13c), .out14(x14c), .out15(x15c),
    .out16(x16c), .out17(x17c), .out18(x18c), .out19(x19c), .out20(x20c), .out21(x21c), .out22(x22c),
    .out23(x23c), .out24(x24c), .out25(x25c), .out26(x26c), .out27(x27c), .out28(x28c), .out29(x29c),
    .out30(x30c), .out31(x31c), .in(RegWEn), .sel(rd));  // open: out0

  // Other names for the same wires on the sheet: read_data1[31:0] = Read_Data_1; read_data2[31:0] = Read_Data_2;
  //   read_reg1[4:0] = rs1; read_reg2[4:0] = rs2; write_en = RegWEn; write_reg[4:0] = rd

  // Notes on the sheet:
  //   INPUTS to your circuit
  //   DON'T CHANGE THE LOCATIONS OF THE INPUTS AND OUTPUTS!
  //   These are DEBUG/TEST outputs from your circuit.
  //   OUTPUTS from your circuit
endmodule
